// Logisim project Lab2_1.circ as structural Verilog: 6 circuits, main circuit main
module main (
  input  A,
  input  B,
  output S,
  output Cout
);

  and and_1 (Cout, A, B);
  xor xor_1 (S, A, B);

  // Notes on the sheet:
  //   Mạch cộng bán phần 
endmodule

module HALFADDER (
  input  in_1,
  input  in_2,
  output out_3,
  output out_4
);

  main main_1 (.A(in_1), .B(in_2), .S(out_3), .Cout(out_4));
endmodule

module FULLADDER (
  input  Cin,
  input  A,
  input  B,
  output S,
  output Cout
);

  wire and_1_out, and_2_out, xor_1_out;

  xor xor_1 (xor_1_out, A, B);
  xor xor_2 (S, xor_1_out, Cin);
  and and_1 (and_1_out, Cin, xor_1_out);
  and and_2 (and_2_out, B, A);
  or or_1 (Cout, and_1_out, and_2_out);
endmodule

module _4_bit_adder (
  input  [3:0] S_4,
  input  Cin,
  input  [3:0] A_4,
  input  [3:0] in_4,
  output Cout
);

  wire fulladder_1_cout, fulladder_2_cout, fulladder_3_cout;
  wire [3:0] fulladder_1_s;

  FULLADDER fulladder_1 (.Cin(Cin), .A(A_4[0]), .B(in_4[0]), .S(fulladder_1_s[0]), .Cout(fulladder_1_cout));
  FULLADDER fulladder_2 (
    .Cin(fulladder_1_cout), .A(A_4[1]), .B(in_4[1]), .S(fulladder_1_s[1]), .Cout(fulladder_2_cout));
  FULLADDER fulladder_3 (
    .Cin(fulladder_2_cout), .A(A_4[2]), .B(in_4[2]), .S(fulladder_1_s[2]), .Cout(fulladder_3_cout));
  FULLADDER fulladder_4 (.Cin(fulladder_3_cout), .A(A_4[3]), .B(in_4[3]), .S(fulladder_1_s[3]), .Cout(Cout));

  // Notes on the sheet:
  //   B[4]
endmodule

module tru_4_bit_adder (
  input  [3:0] S_4,
  input  [3:0] A_4,
  input  [3:0] B_4,
  input  in_4,
  output out_5
);

  wire fulladder_1_cout, fulladder_2_cout, fulladder_3_cout, xor_1_out, xor_2_out, xor_3_out, xor_4_out;
  wire [3:0] fulladder_1_s;

  xor xor_1 (xor_1_out, in_4, B_4[0]);
  xor xor_2 (xor_2_out, in_4, B_4[1]);
  xor xor_3 (xor_3_out, in_4, B_4[2]);
  xor xor_4 (xor_4_out, B_4[3], in_4);
  FULLADDER fulladder_1 (.Cin(in_4), .A(A_4[0]), .B(xor_1_out), .S(fulladder_1_s[0]), .Cout(fulladder_1_cout));
  FULLADDER fulladder_2 (
    .Cin(fulladder_1_cout), .A(A_4[1]), .B(xor_2_out), .S(fulladder_1_s[1]), .Cout(fulladder_2_cout));
  FULLADDER fulladder_3 (
    .Cin(fulladder_2_cout), .A(A_4[2]), .B(xor_3_out), .S(fulladder_1_s[2]), .Cout(fulladder_3_cout));
  FULLADDER fulladder_4 (.Cin(fulladder_3_cout), .A(A_4[3]), .B(xor_4_out), .S(fulladder_1_s[3]), .Cout(out_5));

  // Notes on the sheet:
  //   Phép trừ
endmodule

module FULLADDER1 (
  input  A,
  input  B,
  input  Cin,
  output S,
  output Cout
);

  wire and_1_out, and_2_out, and_3_out, and_4_out, and_5_out, and_6_out, and_7_out, not_1_out, not_2_out,
       not_3_out, not_4_out, not_5_out, not_6_out;

  not not_1 (not_1_out, A);
  not not_2 (not_2_out, B);
  not not_3 (not_3_out, A);
  not not_4 (not_4_out, Cin);
  not not_5 (not_5_out, B);
  not not_6 (not_6_out, Cin);
  and and_1 (and_1_out, B, Cin);
  and and_2 (and_2_out, A, Cin);
  and and_3 (and_3_out, A, B);
  and and_4 (and_4_out, not_1_out, not_2_out, Cin);
  and and_5 (and_5_out, not_3_out, B, not_4_out);
  and and_6 (and_6_out, A, not_5_out, not_6_out);
  and and_7 (and_7_out, A, B, Cin);
  or or_1 (Cout, and_1_out, and_2_out, and_3_out);
  or or_2 (S, and_4_out, and_5_out, and_6_out, and_7_out);
endmodule
