// Logisim project 502044_N15T01_52100174_TranQuangDang_Tuan3.circ as structural Verilog: 5 circuits, main circuit Half Adder
module Half_Adder (
  input  x,
  input  y,
  output C,
  output S
);

  wire and_2_out, and_3_out, not_1_out, not_2_out;

  not not_1 (not_1_out, x);
  not not_2 (not_2_out, y);
  and and_1 (C, x, y);
  and and_2 (and_2_out, not_1_out, y);
  and and_3 (and_3_out, x, not_2_out);
  or or_1 (S, and_2_out, and_3_out);

  // Notes on the sheet:
  //   Half Adder
endmodule

module Full_Adder (
  input  X,
  input  Y,
  input  Z,
  output S,
  output C
);

  wire and_1_out, and_2_out, and_3_out, and_4_out, and_5_out, and_6_out, and_7_out, not_1_out, not_2_out,
       not_3_out, not_4_out, not_5_out, not_6_out;

  not not_1 (not_1_out, X);
  not not_2 (not_2_out, Y);
  not not_3 (not_3_out, X);
  not not_4 (not_4_out, Z);
  not not_5 (not_5_out, Y);
  not not_6 (not_6_out, Z);
  and and_1 (and_1_out, Y, Z);
  and and_2 (and_2_out, X, Z);
  and and_3 (and_3_out, X, Y);
  and and_4 (and_4_out, not_1_out, not_2_out, Z);
  and and_5 (and_5_out, not_3_out, Y, not_4_out);
  and and_6 (and_6_out, X, not_5_out, not_6_out);
  and and_7 (and_7_out, X, Y, Z);
  or or_1 (C, and_1_out, and_2_out, and_3_out);
  or or_2 (S, and_4_out, and_5_out, and_6_out, and_7_out);

  // Notes on the sheet:
  //   Full Adder
endmodule

module SR_Flip_Flop (
  input  S,
  input  R,
  output Q_prime,
  output Q
);

  nor nor_1 (Q_prime, S, Q);
  nor nor_2 (Q, Q_prime, R);

  // Notes on the sheet:
  //   SR Flip-Flop
endmodule

module Led_7_segments (
  input  a,
  input  b,
  input  c,
  input  d,
  output D0,
  output D1,
  output D2,
  output D3,
  output D4,
  output D5,
  output D6
);

  wire and_1_out, and_2_out, and_3_out, and_4_out, and_5_out, and_6_out, and_7_out, and_8_out, and_9_out,
       and_10_out, and_11_out, and_12_out, and_13_out, and_14_out, and_15_out, and_16_out, and_17_out,
       and_18_out, and_19_out, and_20_out, and_21_out, and_22_out, and_23_out, and_24_out, and_25_out,
       and_26_out, and_27_out, and_28_out, and_29_out, and_30_out, and_31_out, not_1_out, not_2_out,
       not_3_out, not_4_out, not_5_out, not_6_out, not_7_out, not_8_out, not_9_out, not_10_out, not_11_out,
       not_12_out, not_13_out, not_14_out, not_15_out, not_16_out, not_17_out, not_18_out, not_19_out,
       not_20_out, not_21_out, not_22_out, not_23_out, not_24_out, not_25_out, not_26_out, not_27_out,
       not_28_out, not_29_out, not_30_out, not_31_out, not_32_out, not_33_out, not_34_out, not_35_out,
       not_36_out, not_37_out, not_38_out, not_39_out, not_40_out;

  not not_1 (not_1_out, a);
  and and_1 (and_1_out, not_1_out, not_2_out, c);
  not not_2 (not_2_out, b);
  not not_3 (not_3_out, a);
  and and_2 (and_2_out, not_3_out, b, not_4_out);
  not not_4 (not_4_out, c);
  and and_3 (and_3_out, b, c, not_5_out);
  not not_5 (not_5_out, d);
  and and_4 (and_4_out, a, not_6_out, not_7_out);
  not not_6 (not_6_out, b);
  not not_7 (not_7_out, c);
  and and_5 (and_5_out, a, c, d);
  not not_8 (not_8_out, c);
  and and_6 (and_6_out, not_8_out, not_9_out);
  not not_9 (not_9_out, d);
  and and_7 (and_7_out, b, not_10_out);
  not not_10 (not_10_out, c);
  and and_8 (and_8_out, b, not_11_out);
  not not_11 (not_11_out, d);
  not not_12 (not_12_out, b);
  and and_9 (and_9_out, not_12_out, not_13_out);
  not not_13 (not_13_out, d);
  not not_14 (not_14_out, a);
  and and_10 (and_10_out, not_14_out, c);
  and and_11 (and_11_out, b, d);
  and and_12 (and_12_out, a, not_15_out);
  not not_15 (not_15_out, c);
  and and_13 (and_13_out, a, not_16_out);
  not not_16 (not_16_out, d);
  not not_17 (not_17_out, a);
  and and_14 (and_14_out, not_17_out, not_18_out, not_19_out);
  not not_18 (not_18_out, c);
  not not_19 (not_19_out, d);
  not not_20 (not_20_out, b);
  and and_15 (and_15_out, not_20_out, not_21_out);
  not not_21 (not_21_out, c);
  not not_22 (not_22_out, b);
  and and_16 (and_16_out, not_22_out, not_23_out);
  not not_23 (not_23_out, d);
  not not_24 (not_24_out, a);
  and and_17 (and_17_out, not_24_out, c, d);
  not not_25 (not_25_out, b);
  and and_18 (and_18_out, not_25_out, not_26_out);
  not not_26 (not_26_out, d);
  and and_19 (and_19_out, c, not_27_out);
  not not_27 (not_27_out, d);
  and and_20 (and_20_out, a, c);
  and and_21 (and_21_out, a, b);
  not not_28 (not_28_out, a);
  not not_29 (not_29_out, b);
  and and_22 (and_22_out, not_28_out, not_29_out, not_30_out);
  not not_30 (not_30_out, d);
  not not_31 (not_31_out, b);
  and and_23 (and_23_out, not_31_out, c, d);
  not not_32 (not_32_out, c);
  and and_24 (and_24_out, b, not_32_out, d);
  and and_25 (and_25_out, b, c, not_33_out);
  not not_33 (not_33_out, d);
  and and_26 (and_26_out, a, not_34_out);
  not not_34 (not_34_out, c);
  not not_35 (not_35_out, a);
  and and_27 (and_27_out, not_35_out, not_36_out);
  not not_36 (not_36_out, c);
  not not_37 (not_37_out, a);
  and and_28 (and_28_out, not_37_out, d);
  not not_38 (not_38_out, c);
  and and_29 (and_29_out, not_38_out, d);
  not not_39 (not_39_out, a);
  and and_30 (and_30_out, not_39_out, b);
  and and_31 (and_31_out, a, not_40_out);
  not not_40 (not_40_out, b);
  or or_1 (D0, and_1_out, and_2_out, and_3_out, and_4_out, and_5_out);
  or or_2 (D1, and_6_out, and_7_out, and_8_out, a);
  or or_3 (D2, and_9_out, and_10_out, and_11_out, and_12_out, and_13_out);
  or or_4 (D3, and_14_out, and_15_out, and_16_out, and_17_out);
  or or_5 (D4, and_18_out, and_19_out, and_20_out, and_21_out);
  or or_6 (D5, and_22_out, and_23_out, and_24_out, and_25_out, and_26_out);
  or or_7 (D6, and_27_out, and_28_out, and_29_out, and_30_out, and_31_out);

  // Notes on the sheet:
  //   Leb 7 segments
endmodule

module main (
  input  x,
  input  y,
  input  in_3,
  input  in_4,
  input  in_5,
  input  in_6,
  input  in_7,
  input  in_8,
  input  in_9,
  input  in_10,
  input  in_11
);

  wire full_adder_1_c, full_adder_1_s, half_adder_1_c, half_adder_1_s, led_7_segments_1_d0,
       led_7_segments_1_d1, led_7_segments_1_d2, led_7_segments_1_d3, led_7_segments_1_d4,
       led_7_segments_1_d5, led_7_segments_1_d6, sr_ff_1_q, sr_ff_1_q_prime;

  Half_Adder half_adder_1 (.x(x), .y(y), .C(half_adder_1_c), .S(half_adder_1_s));
  Full_Adder full_adder_1 (.X(in_3), .Y(in_4), .Z(in_5), .S(full_adder_1_s), .C(full_adder_1_c));
  SR_Flip_Flop sr_ff_1 (.S(in_6), .R(in_7), .Q_prime(sr_ff_1_q_prime), .Q(sr_ff_1_q));
  Led_7_segments led_7_segments_1 (
    .a(in_8), .b(in_9), .c(in_10), .d(in_11), .D0(led_7_segments_1_d0), .D1(led_7_segments_1_d1),
    .D2(led_7_segments_1_d2), .D3(led_7_segments_1_d3), .D4(led_7_segments_1_d4), .D5(led_7_segments_1_d5),
    .D6(led_7_segments_1_d6));
  LED led_1 (.in(half_adder_1_c));
  LED led_2 (.in(half_adder_1_s));
  LED led_3 (.in(full_adder_1_s));
  LED led_4 (.in(full_adder_1_c));
  LED led_5 (.in(sr_ff_1_q_prime));
  LED led_6 (.in(sr_ff_1_q));
  _7_Segment_Display u_7_segment_display_1 (
    .g(led_7_segments_1_d0), .f(led_7_segments_1_d1), .a(led_7_segments_1_d2), .b(led_7_segments_1_d3),
    .e(led_7_segments_1_d4), .d(led_7_segments_1_d5), .c(led_7_segments_1_d6));  // open: dp

  // Notes on the sheet:
  //   Full Adder
  //   Half Adder
  //   SR Flip Flop
  //   LED
  //   LED
endmodule
