// Logisim project BAI2.circ as structural Verilog: 6 circuits, main circuit Cau1
module Cau1 (
  input  in_1,
  input  in_2,
  input  in_3,
  input  in_4,
  input  [3:0] in_5
);

  wire [3:0] undriven;

  Hex_Digit_Display hex_digit_display_1 (.value(undriven));  // open: dp
  LED led_1 ();  // open: in
  LED led_2 ();  // open: in
  LED led_3 ();  // open: in
  Hex_Digit_Display hex_digit_display_2 (.value(in_5));  // open: dp
  LED led_4 ();  // open: in
endmodule

module Cau2 (
  input  a,
  input  b,
  output s,
  output c
);

  xor xor_1 (s, a, b);
  and and_1 (c, a, b);
endmodule

module Mach_chinh_cau_2 (
  input  in_1,
  input  in_2
);

  wire cau2_1_c, cau2_1_s;

  Cau2 cau2_1 (.a(in_1), .b(in_2), .s(cau2_1_s), .c(cau2_1_c));
  LED led_1 (.in(cau2_1_s));
  LED led_2 (.in(cau2_1_c));
endmodule

module Cau_3 (
  input  a,
  input  b,
  output x,
  output y
);

  wire and_1_out, and_2_out, not_1_out, not_2_out, not_3_out;

  not not_1 (not_1_out, b);
  not not_2 (not_2_out, a);
  not not_3 (not_3_out, b);
  or or_1 (x, not_1_out, a);
  and and_1 (and_1_out, not_2_out, b);
  and and_2 (and_2_out, a, not_3_out);
  or or_2 (y, and_1_out, and_2_out);
endmodule

module Cau_4 (
  input  in_1
);

  Clock clock_1 (.out(in_1));
  LED led_1 (.in(in_1));
  LED led_2 (.in(in_1));
  LED led_3 (.in(in_1));
endmodule

module Traffic_Led (
);

  wire clock_1_out;
  wire [2:0] counter_1_q, rom_1_data;

  Clock clock_1 (.out(clock_1_out));
  Counter #(.width(3), .max('h7)) counter_1 (
    .count(clock_1_out), .Q(counter_1_q), .clk(clock_1_out));  // open: load, D, carry, clr
  ROM #(.addrWidth(3), .dataWidth(3)) rom_1 (.addr(counter_1_q), .data(rom_1_data));  // open: sel
  LED led_1 (.in(rom_1_data[0]));
  LED led_2 (.in(rom_1_data[1]));
  LED led_3 (.in(rom_1_data[2]));

  // Notes on the sheet:
  //   contents of rom_1 (hex, n*v repeats v):
  //   1 1 4 4 2 2 1 1
endmodule
